# Fritzing sketch Robot_Fritzing (saved by Fritzing 1.0.1rc)

parts:
  Part1 = Adafruit Motor/Stepper/Servo Shield [part_number="Adafruit #1438"]
  M1 = DC Motor [voltage_(max)=6V voltage_(min)=3V]
  M2 = DC Motor [voltage_(max)=6V voltage_(min)=3V]
  M3 = DC Motor [voltage_(max)=6V voltage_(min)=3V]
  M4 = DC Motor [voltage_(max)=6V voltage_(min)=3V]
  Part2 = Arduino Uno (Rev3) - ICSP
  J1 = Basic Servo
  HC-SR04_Sensor_1 = HC-SR04 Ultrasonic Distance Sensor
  BAT1 = BC9VPC [package=bc9vpc]
  S1 = Square Pushbutton
  U1 = TRANSCHIPTC5747 [package=camera_sfv24r-2st_2]

nets:
  VCC: Part1.AD1, Part1.+5V, Part2.A1, Part2.5V, J1.vcc, HC-SR04_Sensor_1.VCC, HC-SR04_Sensor_1.TRIG
  N1: Part1.AD0, Part2.A0, HC-SR04_Sensor_1.ECHO
  N2: Part1.M2A, M1.pin_2
  N3: Part1.M2B, M1.pin_1
  N4: Part1.M1B, M2.pin_2
  N5: Part1.M1A, M2.pin_1
  N6: Part1.M3A, M4.pin_2
  N7: Part1.M3B, M4.pin_1
  N8: Part1.M4B, M3.pin_2
  N9: Part1.M4A, M3.pin_1
  GND: Part1.GND, Part2.GND, J1.gnd, HC-SR04_Sensor_1.GND, BAT1.V-
  N10: Part1.D11, Part2.D11_PWM/MOSI
  N11: Part1.AD5/SCL, Part2.A5/SCL
  N12: Part1.AD4/SDA, Part2.A4/SDA
  N13: Part1.VMOTOR, S1.leg1
  N14: Part1.D10, Part2.D10_PWM/SS, J1.pulse
  +3V3: Part1.+3V3, Part2.3V3
  N15: Part1.AD2, Part2.A2
  N16: Part1.AD3, Part2.A3
  N17: Part1.AREF, Part2.AREF
  N18: Part1.D1, Part2.D1/TX
  N19: Part1.D2, Part2.D2
  N20: Part1.D3, Part2.D3_PWM
  N21: Part1.D4, Part2.D4
  N22: Part1.D5, Part2.D5_PWM
  N23: Part1.D6, Part2.D6_PWM
  N24: Part1.D7, Part2.D7
  N25: Part1.D8, Part2.D8
  N26: Part1.D9, Part2.D9_PWM
  N27: Part1.D12, U1.DOUT_1
  N28: Part1.D13, Part2.D13/SCK
  N29: Part1./RST, Part2.RESET
  VIN: Part1.VIN, Part2.VIN
  N30: Part2.D0/RX, U1.DOUT_0
  N31: BAT1.V+, S1.leg0

custom parts:
  Adafruit Motor/Stepper/Servo Shield: The original Adafruit Motorshield kit is one of our most beloved kits, which is why we decided to make something even better. We have upgraded the shield kit to make the bestest, easiest way to drive DC and Stepper motors. This shield will make quick work of your next robotics project! We kept the ability to drive up to 4 DC motors or 2 stepper motors, but added many improvements: Instead of a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

// code stored in the sketch: CODE.ino
#include <AFMotor.h>      //add Adafruit Motor Shield library
#include <Servo.h>        //add Servo Motor library            
#include <NewPing.h>      //add Ultrasonic sensor library

#define TRIG_PIN A0 // Pin A0 on the Motor Drive Shield soldered to the ultrasonic sensor
#define ECHO_PIN A1 // Pin A1 on the Motor Drive Shield soldered to the ultrasonic sensor
#define MAX_DISTANCE 300 // sets maximum useable sensor measuring distance to 300cm
#define MAX_SPEED 160 // sets speed of DC traction motors to 150/250 or about 70% of full speed - to get power drain down.
#define MAX_SPEED_OFFSET 40 // this sets offset to allow for differences between the two DC traction motors
#define COLL_DIST 30 // sets distance at which robot stops and reverses to 30cm
#define TURN_DIST COLL_DIST+20 // sets distance at which robot veers away from object
NewPing sonar(TRIG_PIN, ECHO_PIN, MAX_DISTANCE); // sets up sensor library to use the correct pins to measure distance.

AF_DCMotor leftMotor1(1, MOTOR12_1KHZ); // create motor #1 using M1 output on Motor Drive Shield, set to 1kHz PWM frequency
AF_DCMotor leftMotor2(2, MOTOR12_1KHZ); // create motor #2, using M2 output, set to 1kHz PWM frequency
AF_DCMotor rightMotor1(3, MOTOR34_1KHZ);// create motor #3, using M3 output, set to 1kHz PWM frequency
AF_DCMotor rightMotor2(4, MOTOR34_1KHZ);// create motor #4, using M4 output, set to 1kHz PWM frequency
Servo myservo;  // create servo object to control a servo 

int leftDistance, rightDistance; //distances on either side
int curDist = 0;
String motorSet = "";
int speedSet = 0;

//-------------------------------------------- SETUP LOOP ----------------------------------------------------------------------------
void setup() {
  myservo.attach(10);  // attaches the servo on pin 10 (SERVO_1 on the Motor Drive Shield to the servo object 
  myservo.write(90); // tells the servo to position at 90-degrees ie. facing forward.
  delay(1000); // delay for one seconds
 }
//------------------------------------------------------------------------------------------------------------------------------------

//---------------------------------------------MAIN LOOP ------------------------------------------------------------------------------
void loop() {
  myservo.write(90);  // move eyes forward
  delay(90);
  curDist = readPing();   // read distance
  if (curDist < COLL_DIST) {changePath();}  // if forward is blocked change direction
  moveForward();  // move forward
  delay(500);
 }
//-------------------------------------------------------------------------------------------------------------------------------------

void changePath() {
  moveStop();   // stop forward movement
  myservo.write(36);  // check distance to the right
    delay(500);
    rightDistance = readPing(); //set right distance
    delay(500);
    myservo.write(144);  // check distace to the left
    delay(700);
    leftDistance = readPing(); //set left distance
    delay(500);
    myservo.write(90); //return to center
    delay(100);
    compareDistance();
  }

  
void compareDistance()   // find the longest distance
{
  if (leftDistance>rightDistance) //if left is less obstructed 
  {
    turnLeft();
  }
  else if (rightDistance>leftDistance) //if right is less obstructed
  {
    turnRight();
  }
   else //if they are equally obstructed
  {
    turnAround();
  }
}


//-------------------------------------------------------------------------------------------------------------------------------------

int readPing() { // read the ultrasonic sensor distance
  delay(70);   
  unsigned int uS = sonar.ping();
  int cm = uS/US_ROUNDTRIP_CM;
  return cm;
}
//-------------------------------------------------------------------------------------------------------------------------------------
void moveStop() {leftMotor1.run(RELEASE); leftMotor2.run(RELEASE); rightMotor1.run(RELEASE); rightMotor2.run(RELEASE);}  // stop the motors.
//-------------------------------------------------------------------------------------------------------------------------------------
void moveForward() {
    motorSet = "FORWARD";
    leftMotor1.run(FORWARD);      // turn it on going forward
    leftMotor2.run(FORWARD);      // turn it on going forward
    rightMotor1.run(FORWARD);     // turn it on going forward
    rightMotor2.run(FORWARD);     // turn it on going forward
  for (speedSet = 0; speedSet < MAX_SPEED; speedSet +=2) // slowly bring the speed up to avoid loading down the batteries too quickly
  {
    leftMotor1.setSpeed(speedSet);
    leftMotor2.setSpeed(speedSet);
    rightMotor1.setSpeed(speedSet); 
    rightMotor2.setSpeed(speedSet);
    delay(5);
  }
}
//-------------------------------------------------------------------------------------------------------------------------------------
void moveBackward() {
    motorSet = "BACKWARD";
    leftMotor1.run(BACKWARD);     // turn it on going backward
    leftMotor2.run(BACKWARD);     // turn it on going backward
    rightMotor1.run(BACKWARD);    // turn it on going backward
    rightMotor2.run(BACKWARD);    // turn it on going backward
  for (speedSet = 0; speedSet < MAX_SPEED; speedSet +=2) // slowly bring the speed up to avoid loading down the batteries too quickly
  {
    leftMotor1.setSpeed(speedSet);
    leftMotor2.setSpeed(speedSet);
    rightMotor1.setSpeed(speedSet); 
    rightMotor2.setSpeed(speedSet); 
    delay(5);
  }
}  
//-------------------------------------------------------------------------------------------------------------------------------------
void turnRight() {
  motorSet = "RIGHT";
  leftMotor1.run(FORWARD);      // turn motor 1 forward
  leftMotor2.run(FORWARD);      // turn motor 2 forward
  rightMotor1.run(BACKWARD);    // turn motor 3 backward
  rightMotor2.run(BACKWARD);    // turn motor 4 backward
  rightMotor1.setSpeed(speedSet+MAX_SPEED_OFFSET);      
  rightMotor2.setSpeed(speedSet+MAX_SPEED_OFFSET);     
  delay(1500); // run motors this way for 1500        
  motorSet = "FORWARD";
  leftMotor1.run(FORWARD);      // set both motors back to forward
  leftMotor2.run(FORWARD);
  rightMotor1.run(FORWARD);
  rightMotor2.run(FORWARD);      
}  
//-------------------------------------------------------------------------------------------------------------------------------------
void turnLeft() {
  motorSet = "LEFT";
  leftMotor1.run(BACKWARD);      // turn motor 1 backward
  leftMotor2.run(BACKWARD);      // turn motor 2 backward
  leftMotor1.setSpeed(speedSet+MAX_SPEED_OFFSET);     
  leftMotor2.setSpeed(speedSet+MAX_SPEED_OFFSET);    
  rightMotor1.run(FORWARD);     // turn motor 3 forward
  rightMotor2.run(FORWARD);     // turn motor 4 forward
  delay(1500); // run motors this way for 1500  
  motorSet = "FORWARD";
  leftMotor1.run(FORWARD);      // turn it on going forward
  leftMotor2.run(FORWARD);      // turn it on going forward
  rightMotor1.run(FORWARD);     // turn it on going forward
  rightMotor2.run(FORWARD);     // turn it on going forward
}  
//-------------------------------------------------------------------------------------------------------------------------------------
void turnAround() {
  motorSet = "RIGHT";
  leftMotor1.run(FORWARD);      // turn motor 1 forward
  leftMotor2.run(FORWARD);      // turn motor 2 forward
  rightMotor1.run(BACKWARD);    // turn motor 3 backward
  rightMotor2.run(BACKWARD);    // turn motor 4 backward
  rightMotor1.setSpeed(speedSet+MAX_SPEED_OFFSET);      
  rightMotor2.setSpeed(speedSet+MAX_SPEED_OFFSET);
  delay(1700); // run motors this way for 1700
  motorSet = "FORWARD";
  leftMotor1.run(FORWARD);      // set both motors back to forward
  leftMotor2.run(FORWARD);
  rightMotor1.run(FORWARD);
  rightMotor2.run(FORWARD);      
}
